# Fritzing sketch Vsens (saved by Fritzing 0.9.1b)
circuit board: 2.98678cm x 2.96611cm
breadboards: 1

parts:
  Part1 = Arduino Uno (Rev3)
  R2 = Resistor [tolerance=±5% resistance=10k package=THT]
  R1 = Resistor [tolerance=±5% resistance=100k package=THT]
  VCC1 = Battery

nets:
  N1: Part1.A0, R2.Pin_0, R1.Pin_1
  N2: Part1.GND, R2.Pin_1, VCC1.-
  N3: R1.Pin_0, VCC1.+
