# Fritzing sketch sensRHT (saved by Fritzing 0.9.1b)
circuit board: 8.46667cm x 5.64444cm
breadboards: 1

parts:
  RHT1 = Humidity and Temperature Sensor RHT03
  R1 = Resistor [tolerance=±5% resistance=1k package=THT]
  Part1 = Arduino Uno (Rev3)

nets:
  VCC: RHT1.Vcc, R1.Pin_0, Part1.5V
  N1: RHT1.Data-signal, R1.Pin_1, Part1.D4
  N2: RHT1.GND_1, RHT1.GND_2, Part1.GND
