# Fritzing sketch sensT (saved by Fritzing 0.9.1b)
breadboards: 1

parts:
  Part1 = Arduino Uno (Rev3)
  DS1 = DS18B20 1-Wire Temperature Sensor Probe Cable
  R1 = Resistor [tolerance=±5% resistance=4.7 package=THT]

nets:
  N1: Part1.D10_PWM/SS, DS1.shield, R1.Pin_1
  3V3: Part1.3V3, DS1.VDD, R1.Pin_0
  GND: Part1.GND, DS1.GND
